# Fritzing sketch 12V_device (saved by Fritzing 0.9.3b)
breadboards: 1

parts:
  R1 = Resistor [tolerance=±5% resistance=10k package=THT]
  Diode = Rectifier Diode [part_number=1N4001 package="300 mil [THT]"]
  R2 = Resistor [tolerance=±5% resistance=220 package=THT]
  Part1 = Arduino Uno (Rev3)
  12V_actuator = DC Motor
  12V_Power_Supply = Power plug
  MOSFET_IRLZ44N = Basic FET N-Channel [package="DPak [SMD]"]

nets:
  N1: R1.Pin_0, R2.Pin_1, MOSFET_IRLZ44N.Gate
  GND: R1.Pin_1, Part1.GND, 12V_Power_Supply.GND, MOSFET_IRLZ44N.source
  N2: Diode.cathode, 12V_actuator.pin_2, 12V_Power_Supply.VCC
  N3: Diode.anode, 12V_actuator.pin_1, MOSFET_IRLZ44N.drain
  N4: R2.Pin_0, Part1.D10_PWM/SS
